// Logisim project circuit.circ as structural Verilog: 1 circuit, main circuit main
module main (
  input  A3,
  input  B3,
  input  A2,
  input  B2,
  input  A1,
  input  B1,
  input  A0,
  input  B0,
  input  C0,
  output R0,
  output R1,
  output R2,
  output R3,
  output C3
);

  wire and_1_out, and_2_out, and_3_out, and_4_out, and_5_out, and_6_out, and_7_out, and_8_out, or_1_out,
       or_2_out, or_3_out, xor_1_out, xor_2_out, xor_3_out, xor_4_out;

  xor xor_1 (xor_1_out, B0, A0);
  and and_1 (and_1_out, B0, A0);
  xor xor_2 (xor_2_out, B1, A1);
  and and_2 (and_2_out, B1, A1);
  xor xor_3 (xor_3_out, B2, A2);
  and and_3 (and_3_out, B2, A2);
  xor xor_4 (xor_4_out, B3, A3);
  and and_4 (and_4_out, B3, A3);
  xor xor_5 (R0, C0, xor_1_out);
  and and_5 (and_5_out, xor_1_out, C0);
  xor xor_6 (R1, or_1_out, xor_2_out);
  and and_6 (and_6_out, xor_2_out, or_1_out);
  xor xor_7 (R2, or_2_out, xor_3_out);
  and and_7 (and_7_out, xor_3_out, or_2_out);
  xor xor_8 (R3, or_3_out, xor_4_out);
  and and_8 (and_8_out, xor_4_out, or_3_out);
  or or_1 (or_1_out, and_1_out, and_5_out);
  or or_2 (or_2_out, and_2_out, and_6_out);
  or or_3 (or_3_out, and_3_out, and_7_out);
  or or_4 (C3, and_4_out, and_8_out);

  // Notes on the sheet:
  //   3
  //   2
  //   3
  //   2
  //   10
  //   9
  //   10
  //   9
  //   17
  //   16
  //   17
  //   16
  //   24
  //   23
  //   24
  //   23
  //   4
  //   6
  //   11
  //   13
  //   18
  //   20
  //   25
  //   27
  //   1
  //   4
  //   4
  //   1
  //   8
  //   11
  //   11
  //   8
  //   15
  //   18
  //   18
  //   15
  //   22
  //   25
  //   25
  //   22
  //   5
  //   7
  //   12
  //   14
  //   19
  //   21
  //   26
  //   28
  //   6
  //   7
  //   13
  //   14
  //   20
  //   21
  //   27
  //   28
  //   8
  //   15
  //   22
  //   29
endmodule
